# Fritzing sketch klimat (saved by Fritzing 0.9.10b)

parts:
  Компонент1 = LCD1602-I2C
  Компонент2 = Arduino Nano (Rev3.0)
  Компонент3 = AHT20 BMP280 pressure and humidity breakout
  Компонент4 = AHT20 BMP280 pressure and humidity breakout
  RTC1 = DS3231 AT24C32 Real Time Clock
  BAT1 = Battery Holders [package=lipo-1100mAh]
  M1 = RioRand LM2596

nets:
  GND: Компонент1.GND, Компонент2.GND, Компонент3.GND, Компонент4.GND, RTC1.GND, M1.Pin_4
  VCC: Компонент1.VCC, Компонент2.5V, Компонент3.VDD, Компонент4.VDD, RTC1.VCC, M1.Pin_3
  N1: Компонент1.SDA, Компонент2.A4, Компонент3.SDA, Компонент4.SCL, Компонент4.SDA, RTC1.SDA
  N2: Компонент1.SCL, Компонент2.A5, Компонент3.SCL, RTC1.SCL
  N3: BAT1.+, M1.Pin_1
  N4: BAT1.-, M1.Pin_2

custom parts:
  LCD1602-I2C: A standard character display, usually with 2x16 characters. Comes in many colors with LCM1602 IIC attached.
  AHT20 BMP280 pressure and humidity breakout: Cheap breakout board for the BMP280, barometric pressure sensor, and AHT20, humidity sensor
  DS3231 AT24C32 Real Time Clock: Real-time clock basedo on chip DS3231, plus memory chip AT24C32 (32 Kb storage capacity). On-chip temperature sensor with an accuracy of ±3 ℃, I2C bus interface maximum speed: 400 kHz. Operating voltage: 3.3 V to 5.5 V with battery backup capabilities.
